# Fritzing sketch model_leds (saved by Fritzing 0.9.2b)
breadboards: 1

parts:
  Part1 = Arduino Uno (Rev3)
  LED1 = LED - 5mm [color="Red (633nm)" package="5 mm [THT]"]
  LED2 = LED - 5mm [color="Red (633nm)" package="5 mm [THT]"]
  LED3 = LED - 5mm [color="Red (633nm)" package="5 mm [THT]"]
  LED4 = LED - 5mm [color="Red (633nm)" package="5 mm [THT]"]
  R1 = Resistor [tolerance=±5% resistance=10 package=THT]
  R2 = Resistor [tolerance=±5% resistance=10 package=THT]
  R3 = Resistor [tolerance=±5% resistance=10 package=THT]
  R4 = Resistor [tolerance=±5% resistance=10 package=THT]

nets:
  N1: Part1.D2, R1.Pin_1
  N2: Part1.D3_PWM, R2.Pin_1
  N3: Part1.D4, R3.Pin_1
  N4: Part1.D5_PWM, R4.Pin_1
  N5: Part1.5V, LED1.cathode, LED2.cathode, LED3.cathode, LED4.cathode
  N6: LED1.anode, R1.Pin_0
  N7: LED2.anode, R2.Pin_0
  N8: LED3.anode, R3.Pin_0
  N9: LED4.anode, R4.Pin_0
